// Logisim project 5-bit Incrementer.circ as structural Verilog: 1 circuit, main circuit main
module main (
  input  in_1,
  input  in_2,
  input  in_3,
  input  in_4,
  input  in_5,
  output out_6,
  output out_7,
  output out_8,
  output out_9,
  output out_10
);

  wire adder_1_cout, adder_2_cout, adder_3_cout, adder_4_cout;

  Adder #(.width(1)) adder_1 (.a(1'b1), .b(in_1), .out(out_6), .cout(adder_1_cout));  // open: cin
  Adder #(.width(1)) adder_2 (.a(adder_1_cout), .b(in_2), .out(out_7), .cout(adder_2_cout));  // open: cin
  Adder #(.width(1)) adder_3 (.a(adder_2_cout), .b(in_3), .out(out_8), .cout(adder_3_cout));  // open: cin
  Adder #(.width(1)) adder_4 (.a(adder_3_cout), .b(in_4), .out(out_9), .cout(adder_4_cout));  // open: cin
  Adder #(.width(1)) adder_5 (.a(adder_4_cout), .b(in_5), .out(out_10));  // open: cin, cout
endmodule
