// Logisim project 8-bit Adder.circ as structural Verilog: 1 circuit, main circuit main
module main (
  input  a7,
  input  a6,
  input  a5,
  input  a4,
  input  a3,
  input  a2,
  input  a1,
  input  a0,
  input  b7,
  input  b6,
  input  b5,
  input  b4,
  input  b3,
  input  b2,
  input  b1,
  input  b0,
  input  cin,
  output cout,
  output out_19,
  output out_20,
  output out_21,
  output out_22,
  output out_23,
  output out_24,
  output out_25,
  output out_26
);

  wire main_2_cout, main_3_cout, main_4_cout, main_5_cout, main_6_cout, main_7_cout, main_8_cout;

  Full_Adder_main main_1 (.a(a7), .b(b7), .cin(main_2_cout), .result(out_19), .cout(cout));
  Full_Adder_main main_2 (.a(a6), .b(b6), .cin(main_3_cout), .result(out_20), .cout(main_2_cout));
  Full_Adder_main main_3 (.a(a5), .b(b5), .cin(main_4_cout), .result(out_21), .cout(main_3_cout));
  Full_Adder_main main_4 (.a(a4), .b(b4), .cin(main_5_cout), .result(out_22), .cout(main_4_cout));
  Full_Adder_main main_5 (.a(a3), .b(b3), .cin(main_6_cout), .result(out_23), .cout(main_5_cout));
  Full_Adder_main main_6 (.a(a2), .b(b2), .cin(main_7_cout), .result(out_24), .cout(main_6_cout));
  Full_Adder_main main_7 (.a(a1), .b(b1), .cin(main_8_cout), .result(out_25), .cout(main_7_cout));
  Full_Adder_main main_8 (.a(a0), .b(b0), .cin(cin), .result(out_26), .cout(main_8_cout));
endmodule
