// Logisim project Bidirectional Bus.circ as structural Verilog: 1 circuit, main circuit main
module main (
  input  [7:0] Address_to_read_from,
  input  Control,
  input  [7:0] Data_to_be_written,
  output [7:0] Data_read,
  output [7:0] Address_to_be_writen_to
);

  wire not_1_out;

  assign Data_read = Control ? Address_to_read_from : 8'bz;  // Controlled_Buffer controlled_buffer_1
  not not_1 (not_1_out, Control);
  assign Address_to_be_writen_to = not_1_out ? Data_to_be_written : 8'bz;  // Controlled_Buffer controlled_buffer_2
endmodule
