// Logisim project CPU.circ as structural Verilog: 1 circuit, main circuit main
module main (
);

  wire and_1_out, clock_1_out, clock_2_out, nand_1_out, nand_2_out, not_1_out, not_2_out, not_3_out,
       not_4_out, not_5_out, not_6_out, not_7_out, Reset_out;
  wire [1:0] rom_1_data_2, rom_1_data_3;
  wire [3:0] rom_1_data;
  wire [4:0] main_2_out_6, register_1_q;
  wire [7:0] main_1_val_a, main_1_val_b, main_3_out_26, main_4_data_read, ram_1_data;

  Clock clock_1 (.out(clock_1_out));
  Button Reset (.out(Reset_out));
  and and_1 (and_1_out, clock_1_out, nand_1_out);
  nand nand_1 (nand_1_out, not_1_out, not_2_out, not_3_out, not_4_out, not_5_out, not_6_out, rom_1_data_2[0], rom_1_data_2[1]);
  Clock clock_2 (.out(clock_2_out));
  Register #(.width(5)) register_1 (.D(main_2_out_6), .Q(register_1_q), .clk(and_1_out), .clr(Reset_out));  // open: en
  not not_1 (not_1_out, rom_1_data[0]);
  not not_2 (not_2_out, rom_1_data[1]);
  not not_3 (not_3_out, rom_1_data[2]);
  not not_4 (not_4_out, rom_1_data[3]);
  not not_5 (not_5_out, rom_1_data_3[0]);
  not not_6 (not_6_out, rom_1_data_3[1]);
  not not_7 (not_7_out, rom_1_data_2[1]);
  nand nand_2 (nand_2_out, not_7_out, rom_1_data_2[0]);
  ROM #(.addrWidth(5)) rom_1 (.addr(register_1_q), .data({rom_1_data_2, rom_1_data_3, rom_1_data}));  // open: sel
  Register_File_main main_1 (
    .Val_B(main_1_val_b), .Val_A(main_1_val_a), .RA(rom_1_data_3[1]), .RB(rom_1_data_3[0]),
    .OP(rom_1_data_2), .Val_M(main_4_data_read), .Val_E(main_3_out_26));
  RAM #(.addrWidth(4)) ram_1 (
    .addr(rom_1_data), .data(ram_1_data), .clk(clock_2_out), .ld(nand_2_out));  // open: sel, clr
  _5_bit_Incrementer_main main_2 (
    .in_1(register_1_q[0]), .in_2(register_1_q[1]), .in_3(register_1_q[2]), .in_4(register_1_q[3]),
    .in_5(register_1_q[4]), .out_6(main_2_out_6[0]), .out_7(main_2_out_6[1]), .out_8(main_2_out_6[2]),
    .out_9(main_2_out_6[3]), .out_10(main_2_out_6[4]));
  _8_bit_Adder_main main_3 (
    .a7(main_1_val_a[7]), .b7(main_1_val_b[7]), .a6(main_1_val_a[6]), .b6(main_1_val_b[6]),
    .a5(main_1_val_a[5]), .b5(main_1_val_b[5]), .a4(main_1_val_a[4]), .b4(main_1_val_b[4]),
    .a3(main_1_val_a[3]), .b3(main_1_val_b[3]), .a2(main_1_val_a[2]), .b2(main_1_val_b[2]),
    .a1(main_1_val_a[1]), .b1(main_1_val_b[1]), .a0(main_1_val_a[0]), .b0(main_1_val_b[0]), .cin(1'b0),
    .out_19(main_3_out_26[7]), .out_20(main_3_out_26[6]), .out_21(main_3_out_26[5]),
    .out_22(main_3_out_26[4]), .out_23(main_3_out_26[3]), .out_24(main_3_out_26[2]),
    .out_25(main_3_out_26[1]), .out_26(main_3_out_26[0]));  // open: cout
  Bidirectional_Bus_main main_4 (
    .Control(nand_2_out), .Address_to_be_writen_to(ram_1_data), .Data_read(main_4_data_read),
    .Data_to_be_written(main_1_val_b), .Address_to_read_from(ram_1_data));

  // Notes on the sheet:
  //   contents of rom_1 (hex, n*v repeats v):
  //   0 24 a0 68 1 25 a0 69 2 26 a0 6a 3 27 a0 6b c0
endmodule
