// Logisim project Full Adder.circ as structural Verilog: 1 circuit, main circuit main
module main (
  input  a,
  input  b,
  input  cin,
  output cout,
  output result
);

  wire and_1_out, and_2_out, and_3_out, xor_1_out;

  and and_1 (and_1_out, a, b);
  and and_2 (and_2_out, b, cin);
  and and_3 (and_3_out, a, cin);
  or or_1 (cout, and_1_out, and_3_out, and_2_out);
  xor xor_1 (xor_1_out, a, b);
  xor xor_2 (result, cin, xor_1_out);
endmodule
