// Logisim project Register File.circ as structural Verilog: 1 circuit, main circuit main
module main (
  input  RA,
  input  RB,
  input  [1:0] OP,
  input  [7:0] Val_M,
  input  [7:0] Val_E,
  output [7:0] Val_B,
  output [7:0] Val_A
);

  wire and_1_out, and_2_out, and_3_out, and_4_out, and_5_out, and_6_out, and_7_out, and_8_out, clock_1_out,
       not_1_out, not_2_out, not_3_out, or_1_out, or_2_out, or_3_out, or_4_out, xor_1_out, xor_2_out;
  wire [7:0] demultiplexer_1_out0, demultiplexer_1_out1, multiplexer_1_out;

  and and_1 (and_1_out, xor_1_out, and_3_out);
  xor xor_1 (xor_1_out, RA, RB);
  not not_1 (not_1_out, RA);
  or or_1 (or_1_out, and_1_out, and_2_out);
  and and_2 (and_2_out, not_1_out, not_2_out);
  not not_2 (not_2_out, OP[1]);
  and and_3 (and_3_out, OP[1], not_3_out);
  not not_3 (not_3_out, OP[0]);
  or or_2 (or_2_out, and_4_out, and_5_out);
  and and_4 (and_4_out, not_2_out, RA);
  and and_5 (and_5_out, and_6_out, xor_2_out);
  and and_6 (and_6_out, OP[1], not_3_out);
  xor xor_2 (xor_2_out, RA, RB);
  or or_3 (or_3_out, not_2_out, not_3_out);
  and and_7 (and_7_out, not_3_out, not_2_out);
  and and_8 (and_8_out, not_3_out, OP[1]);
  Register register_1 (.D(demultiplexer_1_out0), .en(or_1_out), .Q(Val_A), .clk(clock_1_out));  // open: clr
  or or_4 (or_4_out, and_7_out, and_8_out);
  Demultiplexer #(.width(8)) demultiplexer_1 (
    .out0(demultiplexer_1_out0), .out1(demultiplexer_1_out1), .in(multiplexer_1_out), .sel(RA), .en(or_3_out));
  Multiplexer #(.width(8)) multiplexer_1 (
    .in0(Val_M), .in1(Val_E), .out(multiplexer_1_out), .sel(and_8_out), .en(or_4_out));
  Register register_2 (.D(demultiplexer_1_out1), .en(or_2_out), .Q(Val_B), .clk(clock_1_out));  // open: clr
  Clock clock_1 (.out(clock_1_out));
endmodule
